# Fritzing sketch module Pengaduk (saved by Fritzing 0.9.3b)
breadboards: 1

parts:
  Part1 = Arduino Mega 2560 (Rev3)
  S1 = PH meter [package=THT]
  IC1 = DIP - 6 pins [chip_label="TDS METER V 1.0" package="DIP (Dual Inline) [THT]"]
  OLED_I2C1 = OLED 128x64 I2C Monochrome Display
  YF-S201_Flow_Meter2 = YF-S201 Water Flow Meter
  A2 = 2 channel relay module [package=THT]
  YF-S201_Flow_Meter3 = YF-S201 Water Flow Meter
  YF-S201_Flow_Meter4 = YF-S201 Water Flow Meter
  YF-S201_Flow_Meter5 = YF-S201 Water Flow Meter
  VALVE1 = Plastic Solenoid Valve
  VALVE2 = Plastic Solenoid Valve
  VALVE3 = Plastic Solenoid Valve
  VALVE4 = Plastic Solenoid Valve
  U1 = 4-Channel 5v Relay Shield [package=relay-4ch5v10a]
  JACK2 = 2.1mm Barrel Jack with Terminal Block
  M1 = JSN-SRO4T [package=THT]

nets:
  N1: Part1.A0, S1.pin1
  VCC: Part1.A1, Part1.5V, S1.pin3, IC1.A, IC1.VCC, OLED_I2C1.VDD, YF-S201_Flow_Meter2.VCC, YF-S201_Flow_Meter5.VCC
  N2: Part1.D21/SCL, OLED_I2C1.SDA
  N3: Part1.D20/SDA, OLED_I2C1.SCK
  N4: Part1.D19/RX1, M1.pin3
  N5: Part1.D18/TX1, M1.pin2
  GND: Part1.GND, S1.pin2, IC1.GND, OLED_I2C1.GND, YF-S201_Flow_Meter2.GND, YF-S201_Flow_Meter5.GND
  N6: Part1.D13_PWM, U1.IN3
  N7: Part1.D12_PWM, U1.IN2
  N8: Part1.D11_PWM, U1.IN1
  N9: Part1.D10_PWM, U1.GND
  N10: Part1.D0_RX0, A2.pin_15
  N11: Part1.D1_TX0, YF-S201_Flow_Meter4.SIG
  N12: Part1.D2_PWM, YF-S201_Flow_Meter5.SIG
  N13: Part1.D3_PWM, YF-S201_Flow_Meter3.SIG
  N14: Part1.D4_PWM, YF-S201_Flow_Meter2.SIG
  N15: VALVE1.no_name_yet#1, U1.K1-In
  N16: VALVE2.no_name_yet#1, U1.K2-Off
  N17: VALVE3.no_name_yet#1, U1.K3-Off
  N18: VALVE4.no_name_yet#1, U1.K4-Off
  N19: VALVE4.no_name_yet#2, JACK2.NEG
  N20: U1.K1-Off, JACK2.POS
  N21: U1.K1-On, U1.K2-In
  N22: U1.K2-On, U1.K3-In
  N23: U1.K3-On, U1.K4-In

notes:
  TSD METER
  PH
  vcc : vcc
  GND : GND
  A : A0
  IN : A0
  GND : GND
  VCC : VCC
  SDA : SDA
  SCL : SCL
  GND : GND
  VCC : VCC
  SOCKET KE TDS
  SOCKET KE PH SENSOR
  GND : GND
  VCC : VCC
  PIN : D4
  GND : GND
  VCC : VCC
  PIN : D3
  GND : GND
  VCC : VCC
  PIN : D2
  GND : GND
  VCC : VCC
  PIN : D6
  KE PENGADUK
  VCC : VCC
  GND : GND
  TRIG : D15
  ECHO : 14
  TRIGGER : 19
  ECHO : 18
  iN1 : 10
  IN2 : 11
  IN3 : 12
  IN4 : 13
  12 V DC

custom parts:
  DIP - 6 pins: A DIP stand-in part for whatever IC you want. With 6 pins on a 300mil dual inline package (DIP) footprint.
  YF-S201 Water Flow Meter: The YF-S201 Flow Meter. The input voltage is 5V to 24V (DC).
  2 channel relay module: 2 channel Relay Module 5V 12V 24V High and Low Level Trigger Relay Control With Optocoupler Two Way relays DC 5 V 12 V 24 V Volt.
  4-Channel 5v Relay Shield: 4 Channel 5v Relay Shield w. 2x SPD-06VDC-SD-C
  JSN-SRO4T: JSN-SR04T Waterproof Ultrasonic Distance Measuring Module Integrated Ultrasonic Detection Module DC 5V.
